// Logisim project Practica05.circ as structural Verilog
// AFD
module automata (
  input  In
);

  wire clock_1_out, E1_qn, E2_qn, not_1_out, R1_out, S1_out, S2_out;
  wire [1:0] E2_q;

  Clock clock_1 (.out(clock_1_out));
  not not_1 (not_1_out, In);
  S_R_Flip_Flop E1 (.S(S1_out), .clk(clock_1_out), .R(R1_out), .Q(E2_q[1]), .Qn(E1_qn));  // open: preset, reset, en
  S_R_Flip_Flop E2 (.S(S2_out), .clk(clock_1_out), .R(E2_q[0]), .Q(E2_q[0]), .Qn(E2_qn));  // open: preset, reset, en
  and S1 (S1_out, E1_qn, E2_q[0], not_1_out);
  and R1 (R1_out, E2_q[1], E2_q[0], not_1_out);
  and S2 (S2_out, E2_qn, not_1_out);
  Hex_Digit_Display hex_digit_display_1 (.value({2'b00, E2_q}));  // open: dp

  // Notes on the sheet:
  //   Entrada del autómata
  //   0 = error
  //   1 = acierto
  //   Autómata del ejercicio 1
  //   R2
  //   Estado actual del autómata.
  //   0 = T
  //   1 = TE
  //   2 = NT
  //   3 = NTE
endmodule

// REG
module registro (
  input  Escribir,
  input  [7:0] Dato_a_escribir,
  output [7:0] \Dato_leído 
);

  D_Flip_Flop d_ff_1 (.clk(Escribir), .D(Dato_a_escribir[0]), .Q(\Dato_leído [0]));  // open: Qn, preset, en, reset
  D_Flip_Flop d_ff_2 (.clk(Escribir), .D(Dato_a_escribir[1]), .Q(\Dato_leído [1]));  // open: Qn, preset, en, reset
  D_Flip_Flop d_ff_3 (.clk(Escribir), .D(Dato_a_escribir[2]), .Q(\Dato_leído [2]));  // open: Qn, preset, en, reset
  D_Flip_Flop d_ff_4 (.clk(Escribir), .D(Dato_a_escribir[3]), .Q(\Dato_leído [3]));  // open: Qn, preset, en, reset
  D_Flip_Flop d_ff_5 (.clk(Escribir), .D(Dato_a_escribir[4]), .Q(\Dato_leído [4]));  // open: Qn, preset, en, reset
  D_Flip_Flop d_ff_6 (.clk(Escribir), .D(Dato_a_escribir[5]), .Q(\Dato_leído [5]));  // open: Qn, preset, en, reset
  D_Flip_Flop d_ff_7 (.clk(Escribir), .D(Dato_a_escribir[6]), .Q(\Dato_leído [6]));  // open: Qn, preset, en, reset
  D_Flip_Flop d_ff_8 (.clk(Escribir), .D(Dato_a_escribir[7]), .Q(\Dato_leído [7]));  // open: Qn, preset, en, reset

  // Notes on the sheet:
  //   Registro de 8 bits usando flip-flop's D
endmodule

module banco (
  input  [1:0] Leer_R1,
  input  [1:0] Escribir_R,
  input  [7:0] Escribir_D,
  input  [1:0] Leer_R2,
  input  Escribir,
  output [7:0] Leer_D1,
  output [7:0] Leer_D2
);

  wire demultiplexer_2_out0, demultiplexer_2_out1, demultiplexer_2_out2, demultiplexer_2_out3;
  wire [7:0] demultiplexer_1_out0, demultiplexer_1_out1, demultiplexer_1_out2, demultiplexer_1_out3,
       \registro_1_dato_leído , \registro_2_dato_leído , \registro_3_dato_leído , \registro_4_dato_leído ;

  Demultiplexer #(.select(2), .width(8), .enable("false")) demultiplexer_1 (
    .out0(demultiplexer_1_out0), .out1(demultiplexer_1_out1), .out2(demultiplexer_1_out2),
    .out3(demultiplexer_1_out3), .in(Escribir_D), .sel(Escribir_R));
  Demultiplexer #(.select(2), .enable("false")) demultiplexer_2 (
    .out0(demultiplexer_2_out0), .out1(demultiplexer_2_out1), .out2(demultiplexer_2_out2),
    .out3(demultiplexer_2_out3), .in(Escribir), .sel(Escribir_R));
  registro registro_1 (
    .Escribir(demultiplexer_2_out0), .Dato_a_escribir(demultiplexer_1_out0),
    .\Dato_leído (\registro_1_dato_leído ));
  registro registro_2 (
    .Escribir(demultiplexer_2_out1), .Dato_a_escribir(demultiplexer_1_out1),
    .\Dato_leído (\registro_2_dato_leído ));
  registro registro_3 (
    .Escribir(demultiplexer_2_out2), .Dato_a_escribir(demultiplexer_1_out2),
    .\Dato_leído (\registro_3_dato_leído ));
  registro registro_4 (
    .Escribir(demultiplexer_2_out3), .Dato_a_escribir(demultiplexer_1_out3),
    .\Dato_leído (\registro_4_dato_leído ));
  Multiplexer #(.select(2), .width(8), .enable("false")) multiplexer_1 (
    .in0(\registro_1_dato_leído ), .in1(\registro_2_dato_leído ), .in2(\registro_3_dato_leído ),
    .in3(\registro_4_dato_leído ), .out(Leer_D1), .sel(Leer_R1));
  Multiplexer #(.select(2), .width(8), .enable("false")) multiplexer_2 (
    .in0(\registro_1_dato_leído ), .in1(\registro_2_dato_leído ), .in2(\registro_3_dato_leído ),
    .in3(\registro_4_dato_leído ), .out(Leer_D2), .sel(Leer_R2));
endmodule
